// Logisim project alu.circ as structural Verilog: 16 circuits, main circuit main
module main (
  input  [31:0] X,
  input  [31:0] Y,
  input  [5:0] Switch__S,
  output Signed_Overflow,
  output [31:0] RESULT,
  output Equal
);

  wire addover, comparator_1_eq, isitaddsub_1_out, select_1_over, subover;
  wire [31:0] add, addu, \and , bitpal, lfsr, \or , sll, slt, sltu, sra, srl, sub, subu;

  sll sll_1 (.X(X), .Y(Y), .out(sll));
  bitpal bitpal_1 (.X(X), .out(bitpal));
  srl srl_1 (.X(X), .Y(Y), .out(srl));
  lfsr lfsr_1 (.X(X), .out(lfsr));
  select select_1 (
    .switch(Switch__S), ._00_sll(sll), ._02_srl(srl), ._03_sra(sra), ._20_add(add), ._21_addu(addu),
    ._22_sub(sub), ._23_subu(subu), ._3e_bitpal(bitpal), ._24_and(\and ), ._25_or(\or ), ._3f_lfsr(lfsr),
    ._2a_slt(slt), ._2b_sltu(sltu), .add_over(addover), .sub_over(subover), .over(select_1_over), .out(RESULT));
  sra sra_1 (.X(X), .Y(Y), .out(sra));
  slt slt_1 (.X(X), .Y(Y), .out(slt));
  addu addu_1 (.X(X), .Y(Y), .out(addu));
  sltu sltu_1 (.X(X), .Y(Y), .out(sltu));
  subu subu_1 (.X(X), .Y(Y), .out(subu));
  \and  and_1 (.X(X), .Y(Y), .out(\and ));
  isitaddsub isitaddsub_1 (.in_1(Switch__S), .out(isitaddsub_1_out));
  Comparator #(.width(32)) comparator_1 (.a(X), .b(Y), .eq(comparator_1_eq));  // open: gt, lt
  add add_1 (.X(X), .Y(Y), .out(add), .out_2(addover));
  \or  or_1 (.X(X), .Y(Y), .out(\or ));
  Multiplexer #(.enable("false")) multiplexer_1 (
    .in0(1'b0), .in1(select_1_over), .out(Signed_Overflow), .sel(isitaddsub_1_out));
  or or_2 (Equal, 1'b0, comparator_1_eq);
  sub sub_1 (.X(X), .Y(Y), .out(subover), .out_2(sub));

  // Other names for the same wires on the sheet: input1[31:0] = X; input2[31:0] = Y; switch[5:0] = Switch__S

  // Notes on the sheet:
  //   INPUTS to your circuit
  //   INPUT to your circuit
  //   DON'T CHANGE THE INPUTS AND OUTPUTS! IF YOU DO SO, YOU NEED TO MAKE SURE THE PINS ARE IN THE RIGHT PLACES!
  //   OUTPUTS of your circuit
endmodule

module select (
  input  add_over,
  input  sub_over,
  input  [31:0] _00_sll,
  input  [31:0] _02_srl,
  input  [31:0] _03_sra,
  input  [31:0] _20_add,
  input  [31:0] _22_sub,
  input  [31:0] _24_and,
  input  [31:0] _2a_slt,
  input  [31:0] _21_addu,
  input  [31:0] _23_subu,
  input  [31:0] _25_or,
  input  [31:0] _2b_sltu,
  input  [31:0] _3e_bitpal,
  input  [31:0] _3f_lfsr,
  input  [5:0] switch,
  output over,
  output [31:0] out
);

  wire multiplexer_5_out, multiplexer_6_out, multiplexer_7_out;
  wire [31:0] multiplexer_1_out, multiplexer_3_out, multiplexer_4_out;

  Multiplexer #(.select(4), .width(32), .enable("false")) multiplexer_1 (
    .in0(_00_sll), .in2(_02_srl), .in3(_03_sra), .out(multiplexer_1_out), .sel(switch[3:0]));  // open: in1, in4, in5, in6, in7, in8, in9, in10, in11, in12, in13, in14, in15
  Multiplexer #(.select(2), .width(32), .enable("false")) multiplexer_2 (
    .in0(multiplexer_1_out), .in2(multiplexer_3_out), .in3(multiplexer_4_out), .out(out), .sel(switch[5:4]));  // open: in1
  Multiplexer #(.select(4), .width(32), .enable("false")) multiplexer_3 (
    .in0(_20_add), .in1(_21_addu), .in2(_22_sub), .in3(_23_subu), .in4(_24_and), .in5(_25_or),
    .in10(_2a_slt), .in11(_2b_sltu), .out(multiplexer_3_out), .sel(switch[3:0]));  // open: in6, in7, in8, in9, in12, in13, in14, in15
  Multiplexer #(.select(4), .width(32), .enable("false")) multiplexer_4 (
    .in14(_3e_bitpal), .in15(_3f_lfsr), .out(multiplexer_4_out), .sel(switch[3:0]));  // open: in0, in1, in2, in3, in4, in5, in6, in7, in8, in9, in10, in11, in12, in13
  Multiplexer #(.enable("false")) multiplexer_5 (.in0(1'b0), .in1(add_over), .out(multiplexer_5_out), .sel(add_over));
  Multiplexer #(.enable("false")) multiplexer_6 (.in0(1'b0), .in1(sub_over), .out(multiplexer_6_out), .sel(sub_over));
  Multiplexer #(.select(4), .enable("false")) multiplexer_7 (
    .in0(multiplexer_5_out), .in1(1'b0), .in2(multiplexer_6_out), .in3(1'b0), .in4(1'b0), .in5(1'b0),
    .in6(1'b0), .in7(1'b0), .in8(1'b0), .in9(1'b0), .in10(1'b0), .in11(1'b0), .in12(1'b0), .in13(1'b0),
    .in14(1'b0), .in15(1'b0), .out(multiplexer_7_out), .sel(switch[3:0]));
  Multiplexer #(.select(2), .enable("false")) multiplexer_8 (
    .in0(1'b0), .in1(1'b0), .in2(multiplexer_7_out), .in3(1'b0), .out(over), .sel(switch[5:4]));
endmodule

module sll (
  input  [31:0] X,
  input  [31:0] Y,
  output [31:0] out
);

  wire [4:0] bit_extender_1_out;

  Bit_Extender #(.in_width(32), .out_width(5)) bit_extender_1 (.in(Y), .out(bit_extender_1_out));
  Shifter #(.width(32)) shifter_1 (.in(X), .\dist (bit_extender_1_out), .out(out));

  // Other names for the same wires on the sheet: input1[31:0] = X; input2[31:0] = Y
endmodule

module srl (
  input  [31:0] X,
  input  [31:0] Y,
  output [31:0] out
);

  wire [4:0] bit_extender_1_out;

  Bit_Extender #(.in_width(32), .out_width(5)) bit_extender_1 (.in(Y), .out(bit_extender_1_out));
  Shifter #(.width(32), .shift("lr")) shifter_1 (.in(X), .\dist (bit_extender_1_out), .out(out));

  // Other names for the same wires on the sheet: input1[31:0] = X; input2[31:0] = Y
endmodule

module sra (
  input  [31:0] X,
  input  [31:0] Y,
  output [31:0] out
);

  wire [4:0] bit_extender_1_out;

  Bit_Extender #(.in_width(32), .out_width(5)) bit_extender_1 (.in(Y), .out(bit_extender_1_out));
  Shifter #(.width(32), .shift("ar")) shifter_1 (.in(X), .\dist (bit_extender_1_out), .out(out));

  // Other names for the same wires on the sheet: input1[31:0] = X; input2[31:0] = Y
endmodule

module add (
  input  [31:0] X,
  input  [31:0] Y,
  output [31:0] out,
  output out_2
);

  wire and_1_out, and_2_out, and_3_out, and_4_out, comparator_1_eq, comparator_2_eq, comparator_3_eq,
       comparator_4_eq, comparator_5_eq, comparator_6_eq;

  Adder #(.width(32)) adder_1 (.a(X), .b(Y), .out(out));  // open: cin, cout
  Comparator #(.width(1)) comparator_1 (.a(X[31]), .b(1'b0), .eq(comparator_1_eq));  // open: gt, lt
  Comparator #(.width(1)) comparator_2 (.a(X[31]), .b(1'b1), .eq(comparator_2_eq));  // open: gt, lt
  Comparator #(.width(1)) comparator_3 (.a(Y[31]), .b(1'b1), .eq(comparator_3_eq));  // open: gt, lt
  Comparator #(.width(1)) comparator_4 (.a(Y[31]), .b(1'b0), .eq(comparator_4_eq));  // open: gt, lt
  and and_1 (and_1_out, comparator_2_eq, comparator_3_eq);
  and and_2 (and_2_out, comparator_1_eq, comparator_4_eq);
  and and_3 (and_3_out, comparator_5_eq, and_1_out);
  Comparator #(.width(1)) comparator_5 (.a(1'b0), .b(out[31]), .eq(comparator_5_eq));  // open: gt, lt
  Comparator #(.width(1)) comparator_6 (.a(1'b1), .b(out[31]), .eq(comparator_6_eq));  // open: gt, lt
  and and_4 (and_4_out, comparator_6_eq, and_2_out);
  or or_1 (out_2, and_3_out, and_4_out);

  // Other names for the same wires on the sheet: input1[31:0] = X; input2[31:0] = Y
endmodule

module addu (
  input  [31:0] X,
  input  [31:0] Y,
  output [31:0] out
);

  Adder #(.width(32)) adder_1 (.a(X), .b(Y), .out(out));  // open: cin, cout

  // Other names for the same wires on the sheet: input1[31:0] = X; input2[31:0] = Y
endmodule

module sub (
  input  [31:0] X,
  input  [31:0] Y,
  output out,
  output [31:0] out_2
);

  wire and_1_out, and_2_out, and_3_out, and_4_out, comparator_1_eq, comparator_2_eq, comparator_3_eq,
       comparator_4_eq, comparator_5_eq, comparator_6_eq;

  Subtractor #(.width(32)) subtractor_1 (.a(X), .b(Y), .out(out_2));  // open: bin, bout
  Comparator #(.width(1)) comparator_1 (.a(1'b1), .b(Y[31]), .eq(comparator_1_eq));  // open: gt, lt
  Comparator #(.width(1)) comparator_2 (.a(1'b1), .b(X[31]), .eq(comparator_2_eq));  // open: gt, lt
  Comparator #(.width(1)) comparator_3 (.a(1'b0), .b(Y[31]), .eq(comparator_3_eq));  // open: gt, lt
  Comparator #(.width(1)) comparator_4 (.a(1'b0), .b(X[31]), .eq(comparator_4_eq));  // open: gt, lt
  and and_1 (and_1_out, comparator_2_eq, comparator_3_eq);
  and and_2 (and_2_out, comparator_4_eq, comparator_1_eq);
  Comparator #(.width(1)) comparator_5 (.a(1'b1), .b(out_2[31]), .eq(comparator_5_eq));  // open: gt, lt
  and and_3 (and_3_out, and_2_out, comparator_5_eq);
  Comparator #(.width(1)) comparator_6 (.a(1'b0), .b(out_2[31]), .eq(comparator_6_eq));  // open: gt, lt
  or or_1 (out, and_3_out, and_4_out);
  and and_4 (and_4_out, comparator_6_eq, and_1_out);

  // Other names for the same wires on the sheet: input1[31:0] = X; input2[31:0] = Y
endmodule

module subu (
  input  [31:0] X,
  input  [31:0] Y,
  output [31:0] out
);

  Subtractor #(.width(32)) subtractor_1 (.a(X), .b(Y), .out(out));  // open: bin, bout

  // Other names for the same wires on the sheet: input1[31:0] = X; input2[31:0] = Y
endmodule

module \and  (
  input  [31:0] X,
  input  [31:0] Y,
  output [31:0] out
);

  assign out = X & Y;  // AND_Gate and_1, 32 bits wide

  // Other names for the same wires on the sheet: input1[31:0] = X; input2[31:0] = Y
endmodule

module \or  (
  input  [31:0] X,
  input  [31:0] Y,
  output [31:0] out
);

  assign out = X | Y;  // OR_Gate or_1, 32 bits wide

  // Other names for the same wires on the sheet: input1[31:0] = X; input2[31:0] = Y
endmodule

module slt (
  input  [31:0] X,
  input  [31:0] Y,
  output [31:0] out
);

  wire comparator_1_lt;

  Comparator #(.width(32)) comparator_1 (.a(X), .b(Y), .lt(comparator_1_lt));  // open: gt, eq
  assign out = {{31{1'b0}}, comparator_1_lt};  // Bit_Extender bit_extender_1

  // Other names for the same wires on the sheet: input1[31:0] = X; input2[31:0] = Y
endmodule

module sltu (
  input  [31:0] X,
  input  [31:0] Y,
  output [31:0] out
);

  wire comparator_1_lt;

  Comparator #(.width(32), .mode("unsigned")) comparator_1 (.a(X), .b(Y), .lt(comparator_1_lt));  // open: gt, eq
  assign out = {{31{1'b0}}, comparator_1_lt};  // Bit_Extender bit_extender_1

  // Other names for the same wires on the sheet: input1[31:0] = X; input2[31:0] = Y
endmodule

module bitpal (
  input  [31:0] X,
  output [31:0] out
);

  wire comparator_1_eq;

  Comparator #(.width(16)) comparator_1 (.a(X[31:16]), .b(X[15:0]), .eq(comparator_1_eq));  // open: gt, lt
  assign out = {{31{1'b0}}, comparator_1_eq};  // Bit_Extender bit_extender_1

  // Other names for the same wires on the sheet: input1[31:0] = X
endmodule

module lfsr (
  input  [31:0] X,
  output [31:0] out
);

  wire xor_1_out, xor_2_out;

  xor xor_1 (xor_1_out, X[0], X[2]);
  xor xor_2 (xor_2_out, X[3], xor_1_out);
  xor xor_3 (out[31], X[5], xor_2_out);

  assign out[30:0] = X[31:1];

  // Other names for the same wires on the sheet: input1[31:0] = X
endmodule

module isitaddsub (
  input  [5:0] in_1,
  output out
);

  wire comparator_1_eq, comparator_2_eq;

  Comparator #(.width(6)) comparator_1 (.a(in_1), .b(6'b100000), .eq(comparator_1_eq));  // open: gt, lt
  Comparator #(.width(6)) comparator_2 (.a(in_1), .b(6'b100010), .eq(comparator_2_eq));  // open: gt, lt
  or or_1 (out, comparator_2_eq, comparator_1_eq);
endmodule
