// Logisim project cpu.circ as structural Verilog: 3 circuits, main circuit main
module main (
  input  [31:0] RS_READ_VALUE,
  input  [31:0] RT_READ_VALUE,
  input  [31:0] INSTRUCTION,
  input  CLOCK,
  input  RESET,
  output [31:0] t0,
  output [31:0] t1,
  output [31:0] t2,
  output [31:0] t3,
  output [4:0] RS,
  output [4:0] RT,
  output [4:0] Write_Register,
  output [31:0] RD_WRITE_VALUE,
  output RD_WRITE_ENABLE,
  output [23:0] FETCH_ADDRESS
);

  // mem_main MEM: pin names not known
  // alu_main ALU: pin names not known
  // regfile_main RegFile: pin names not known

  // Notes on the sheet:
  //   These are outputs/inputs from run.circ
  //   These are outputs to run.circ
  //   Feel free to move these components
endmodule

module control (
  input  [11:0] in_1,
  output jump,
  output jal,
  output regdst,
  output ALUsrc,
  output memtoReg,
  output WriteReg,
  output ReadMem,
  output WriteMem,
  output Branch,
  output OPALU1,
  output OPALU0
);

  and and_1 (OPALU1, ~in_1[11], ~in_1[10], ~in_1[9], ~in_1[8], ~in_1[7], ~in_1[6]);  // AND_Gate
  and and_2 (memtoReg, in_1[11], ~in_1[10], ~in_1[9], ~in_1[8], in_1[7], in_1[6]);  // AND_Gate
  and and_3 (WriteMem, in_1[11], ~in_1[10], in_1[9], ~in_1[8], in_1[7], in_1[6]);  // AND_Gate
  and and_4 (Branch, ~in_1[11], ~in_1[10], ~in_1[9], in_1[8], ~in_1[7], ~in_1[6]);  // AND_Gate
  or or_1 (ALUsrc, memtoReg, WriteMem);
  or or_2 (WriteReg, OPALU1, memtoReg);
  and and_5 (jump, ~in_1[11], ~in_1[10], ~in_1[9], ~in_1[8], in_1[7], ~in_1[6]);  // AND_Gate
  and and_6 (jal, ~in_1[11], ~in_1[10], ~in_1[9], ~in_1[8], in_1[7], in_1[6]);  // AND_Gate

  assign OPALU0 = Branch;
  assign ReadMem = memtoReg;
  assign regdst = OPALU1;

  // Other names for the same wires on the sheet: switch[5:0] = in_1[5:0]
endmodule

module next_PC_Logic (
  input  [23:0] in_1,
  input  [23:0] in_2,
  input  [15:0] immediate,
  input  jump
);

  wire and_1_out, Branch;
  wire [19:0] bit_extender_1_out;
  wire [23:0] adder_1_out, bit_extender_2_out, multiplexer_1_out, multiplexer_2_out, shifter_1_out,
       shifter_2_out;

  Multiplexer #(.width(24), .enable("false")) multiplexer_1 (
    .in0({in_1[23:20], bit_extender_1_out}), .in1(multiplexer_2_out), .out(multiplexer_1_out), .sel(jump));
  Shifter #(.width(24)) shifter_1 (.in(in_2), .\dist (5'b00010), .out(shifter_1_out));
  Bit_Extender #(.in_width(24), .out_width(20)) bit_extender_1 (.in(shifter_1_out), .out(bit_extender_1_out));
  assign bit_extender_2_out = {{8{1'b0}}, immediate};  // Bit_Extender bit_extender_2
  Adder #(.width(24)) adder_1 (.a(in_1), .b(shifter_2_out), .out(adder_1_out));  // open: cin, cout
  Shifter #(.width(24)) shifter_2 (.in(bit_extender_2_out), .\dist (5'b00010), .out(shifter_2_out));
  Multiplexer #(.width(24), .enable("false")) multiplexer_2 (
    .in0(in_1), .in1(adder_1_out), .out(multiplexer_2_out), .sel(and_1_out));
  and and_1 (and_1_out, 1'b0, Branch);
endmodule
