// Logisim project mem.circ as structural Verilog: 1 circuit, main circuit main
module main (
  input  [31:0] Data_Mem_Addr,
  input  [31:0] Data_Mem_In,
  input  ACCESS_BYTE,
  input  MEM_WRITE,
  input  CLOCK,
  output [31:0] Data_Mem_Out
);

  wire not_1_out;
  wire [1:0] lb_selector;
  wire [7:0] lb1, lb2, lb3, lb4, multiplexer_1_out;
  wire [23:0] bit_extender_1_out;
  wire [31:0] bit_extender_2_out, shifter_1_out, shifter_2_out, shifter_3_out, subtractor_1_out;

  assign {lb1, lb2, lb3, lb4} = MEM_WRITE ? Data_Mem_In : 32'bz;  // Controlled_Buffer controlled_buffer_1
  Subtractor #(.width(32)) subtractor_1 (
    .a(Data_Mem_Addr), .b(32'h10010000), .out(subtractor_1_out));  // open: bin, bout
  Shifter #(.width(32)) shifter_1 (.in(subtractor_1_out), .\dist (5'b00100), .out(shifter_1_out));
  Shifter #(.width(32), .shift("lr")) shifter_2 (.in(shifter_1_out), .\dist (5'b01000), .out(shifter_2_out));
  Bit_Extender #(.in_width(32), .out_width(24)) bit_extender_1 (.in(shifter_2_out), .out(bit_extender_1_out));
  not not_1 (not_1_out, MEM_WRITE);
  RAM #(.addrWidth(24), .dataWidth(32)) ram_1 (
    .addr(bit_extender_1_out), .data({lb1, lb2, lb3, lb4}), .sel(1'b1), .clk(CLOCK), .ld(not_1_out));  // open: clr
  Multiplexer #(.select(2), .width(8), .enable("false")) multiplexer_1 (
    .in0(lb1), .in1(lb2), .in2(lb3), .in3(lb4), .out(multiplexer_1_out), .sel(lb_selector));
  assign bit_extender_2_out = {{24{1'b0}}, multiplexer_1_out};  // Bit_Extender bit_extender_2
  Shifter #(.width(32), .shift("lr")) shifter_3 (.in({lb1, lb2, lb3, lb4}), .\dist (5'b11101), .out(shifter_3_out));
  Bit_Extender #(.in_width(32), .out_width(2)) bit_extender_3 (.in(shifter_3_out), .out(lb_selector));
  Multiplexer #(.width(32), .enable("false")) multiplexer_2 (
    .in0({lb1, lb2, lb3, lb4}), .in1(bit_extender_2_out), .out(Data_Mem_Out), .sel(ACCESS_BYTE));

  // Notes on the sheet:
  //   These are INPUTS to the circuit
  //   These are INPUTS to the circuit
  //   DO NOT CHANGE THE LOCATIONS OF THE INPUTS/OUTPUTS! IF YOU DO SO, YOU NEED TO MAKE SURE THE PINS ARE AT THE RIGHT PLACE!
  //   Yet again, the clock is not an actual clock, but an input, one that will be driven from a higher circuit
  //   This is an OUTPUT to the circuit
endmodule
