// Logisim project regfile.circ as structural Verilog: 4 circuits, main circuit main
module main (
  input  [1:0] Read_register_1,
  input  [1:0] Read_register_2,
  input  [1:0] write_register,
  input  [31:0] write_data,
  input  RegWrite,
  input  clock,
  output [31:0] t0_Value,
  output [31:0] t1_Value,
  output [31:0] t2_Value,
  output [31:0] t3_Value,
  output [31:0] Read_Data_1,
  output [31:0] Read_Data_2
);

  wire [1:0] read_1, read_2, readorwrite_1_writeout;
  wire [31:0] readorwrite_1_dataout, t0, t1, t2, t3;

  Register #(.width(32)) u_t0 (.D(t0), .Q(t0_Value), .clk(clock));  // open: en, clr
  readOrWrite readorwrite_1 (
    .read1(Read_register_1), .read2(Read_register_2), .write(write_register), .data(write_data),
    .readorwrite(RegWrite), .read1out(read_1), .read2out(read_2), .writeout(readorwrite_1_writeout),
    .dataout(readorwrite_1_dataout));
  writeData writedata_1 (
    .write_register(readorwrite_1_writeout), .write_data(readorwrite_1_dataout), .t0_Value(t0),
    .t1_Value(t1), .t2_Value(t2), .t3_Value(t3));
  Register #(.width(32)) u_t1 (.D(t1), .Q(t1_Value), .clk(clock));  // open: en, clr
  Register #(.width(32)) u_t2 (.D(t2), .Q(t2_Value), .clk(clock));  // open: en, clr
  Register #(.width(32)) u_t3 (.D(t3), .Q(t3_Value), .clk(clock));  // open: en, clr
  select_out select_out_1 (
    .select(read_1), .t0(t0_Value), .t1(t1_Value), .t2(t2_Value), .t3(t3_Value), .out(Read_Data_1));
  select_out select_out_2 (
    .select(read_2), .t0(t0_Value), .t1(t1_Value), .t2(t2_Value), .t3(t3_Value), .out(Read_Data_2));

  // Other names for the same wires on the sheet: t0_out[31:0] = t0_Value; t1_out[31:0] = t1_Value;
  //   t2_out[31:0] = t2_Value; t3_out[31:0] = t3_Value

  // Notes on the sheet:
  //   These are INPUTS to the circuit
  //   These are INPUTS to the circuit
  //   DO NOT CHANGE THE LOCATIONS OF THE INPUTS/OUTPUTS! IF YOU DO SO, YOU NEED TO MAKE SURE THE PINS ARE AT THE RIGHT PLACE!
  //   These are OUTPUTS to the circuit
  //   Yet again, the clock is not an actual clock, but an input, one that will be driven from a higher circuit
  //   These are OUTPUTS to the circuit
endmodule

module select_out (
  input  [31:0] t0,
  input  [31:0] t1,
  input  [31:0] t2,
  input  [31:0] t3,
  input  [1:0] select,
  output [31:0] out
);

  wire [31:0] multiplexer_1_out, multiplexer_3_out;

  Multiplexer #(.width(32), .enable("false")) multiplexer_1 (
    .in0(t0), .in1(t1), .out(multiplexer_1_out), .sel(select[0]));
  Multiplexer #(.width(32), .enable("false")) multiplexer_2 (
    .in0(multiplexer_1_out), .in1(multiplexer_3_out), .out(out), .sel(select[1]));
  Multiplexer #(.width(32), .enable("false")) multiplexer_3 (
    .in0(t2), .in1(t3), .out(multiplexer_3_out), .sel(select[0]));
endmodule

module writeData (
  input  [1:0] write_register,
  input  [31:0] write_data,
  output [31:0] t0_Value,
  output [31:0] t1_Value,
  output [31:0] t2_Value,
  output [31:0] t3_Value
);

  wire [31:0] multiplexer_1_out, multiplexer_3_out, multiplexer_5_out, multiplexer_7_out;

  Multiplexer #(.width(32), .enable("false")) multiplexer_1 (
    .in0(write_data), .out(multiplexer_1_out), .sel(write_register[0]));  // open: in1
  Multiplexer #(.width(32), .enable("false")) multiplexer_2 (
    .in0(multiplexer_1_out), .out(t0_Value), .sel(write_register[1]));  // open: in1
  Multiplexer #(.width(32), .enable("false")) multiplexer_3 (
    .in0(write_data), .out(multiplexer_3_out), .sel(write_register[0]));  // open: in1
  Multiplexer #(.width(32), .enable("false")) multiplexer_4 (
    .in1(multiplexer_3_out), .out(t2_Value), .sel(write_register[1]));  // open: in0
  Multiplexer #(.width(32), .enable("false")) multiplexer_5 (
    .in1(write_data), .out(multiplexer_5_out), .sel(write_register[0]));  // open: in0
  Multiplexer #(.width(32), .enable("false")) multiplexer_6 (
    .in0(multiplexer_5_out), .out(t1_Value), .sel(write_register[1]));  // open: in1
  Multiplexer #(.width(32), .enable("false")) multiplexer_7 (
    .in1(write_data), .out(multiplexer_7_out), .sel(write_register[0]));  // open: in0
  Multiplexer #(.width(32), .enable("false")) multiplexer_8 (
    .in1(multiplexer_7_out), .out(t3_Value), .sel(write_register[1]));  // open: in0
endmodule

module readOrWrite (
  input  [1:0] read1,
  input  [1:0] read2,
  input  [1:0] write,
  input  [31:0] data,
  input  readorwrite,
  output [1:0] read1out,
  output [1:0] read2out,
  output [1:0] writeout,
  output [31:0] dataout
);

  Multiplexer #(.width(2), .enable("false")) multiplexer_1 (
    .in1(write), .out(writeout), .sel(readorwrite));  // open: in0
  Multiplexer #(.width(32), .enable("false")) multiplexer_2 (
    .in1(data), .out(dataout), .sel(readorwrite));  // open: in0

  assign read1out = read1;
  assign read2out = read2;
endmodule
